# Fritzing sketch mBotstopwatch (saved by Fritzing 0.9.3b)
breadboards: 1

parts:
  Part1 = Robotdyn Nano (Rev3.0)
  RobotDyn1 = 4-Digit LED Display
  S1 = Pushbutton [package="[SMD]"]
  S2 = Pushbutton [package="[SMD]"]
  R1 = Resistor [tolerance=±5% resistance=10k package=THT]
  R2 = Resistor [tolerance=±5% resistance=10k package=THT]
  BAT1 = BC9VPC [package=bc9vpc]
  M1 = fc-51 [package=THT]

nets:
  GND: Part1.GND, RobotDyn1.GND, S1.Pin_1, S1.Pin_2, S2.Pin_1, S2.Pin_2, BAT1.V-, M1.pin2
  N1: Part1.D2, RobotDyn1.CLK
  N2: Part1.D3, RobotDyn1.DIO
  N3: Part1.D6, M1.pin1
  N4: Part1.VIN, BAT1.V+
  5V: Part1.5V, RobotDyn1.VCC, M1.pin3
  N5: Part1.A4, R2.Pin_1
  N6: S1.Pin_3, S1.Pin_4, R1.Pin_0
  N7: S2.Pin_3, S2.Pin_4, R1.Pin_1, R2.Pin_0

custom parts:
  Robotdyn Nano (Rev3.0): The Robotdyn Nano v3.0 is a small, complete, and breadboard-friendly board based on the ATmega328 100% compatible with the Arduino Nano 3.0. It works with a Micro USB cable and brings an independent 3.3 V regulator capable of delivering upt to 500 mA (10x more than the original Arduino Nano).
  4-Digit LED Display: A 4-digit 7-segments LED display
